# Fritzing sketch Calabaza_Fritzing (saved by Fritzing 0.9.0b)
breadboards: 1

parts:
  Raspberry_Pi_B_rev1 = Raspberry Pi B rev1
  LED1 = LED - 5mm [color="Red (633nm)" package="5 mm [THT]"]
  LED2 = LED - 5mm [color="Red (633nm)" package="5 mm [THT]"]
  LED3 = LED - 5mm [color="Red (633nm)" package="5 mm [THT]"]
  LED4 = LED - 5mm [color="Red (633nm)" package="5 mm [THT]"]
  PIR1 = PIR sensor

nets:
  5V: Raspberry_Pi_B_rev1.5V, PIR1.VDD
  GND: Raspberry_Pi_B_rev1.GND, LED4.cathode, PIR1.GND
  N1: Raspberry_Pi_B_rev1.GPIO_23, LED1.cathode, LED2.anode
  N2: Raspberry_Pi_B_rev1.GPIO_18, PIR1.SIG
  N3: Raspberry_Pi_B_rev1.GPIO_22, LED1.anode
  N4: Raspberry_Pi_B_rev1.GPIO_24, LED2.cathode, LED3.anode
  N5: Raspberry_Pi_B_rev1.GPIO_25, LED3.cathode, LED4.anode
